# Fritzing sketch chernila_fritzing (saved by Fritzing 1.0.1rc)

parts:
  SparkFun_ESP32_Thing1 = SparkFun ESP32 Thing [part_number=DEV-13907]
  LED1 = prefix0000
  M1 = MakerFocus MAX30102
  U2 = LIPO-110mAh [package=lipo-110]

nets:
  N1: SparkFun_ESP32_Thing1.VUSB-RAW, LED1.connector1
  N2: SparkFun_ESP32_Thing1.V_BATT, U2.+
  GND: SparkFun_ESP32_Thing1.GND, LED1.connector3, M1.GND, U2.-
  N3: SparkFun_ESP32_Thing1.12, LED1.connector2
  N4: SparkFun_ESP32_Thing1.22, M1.SCL
  N5: SparkFun_ESP32_Thing1.21, M1.SDA

custom parts:
  SparkFun ESP32 Thing: The SparkFun ESP32 Thing is a comprehensive development platform for Espressif’s ESP32, their super-charged version of the popular ESP8266. Like the 8266, the ESP32 is a WiFi-compatible microcontroller, but to that it adds support for Bluetooth low-energy (i.e BLE, BT4.0, Bluetooth Smart), and nearly 30 I/O pins. The ESP32’s power and versatility will make it the foundation of IoT and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
  MakerFocus MAX30102: Oximeter module using the MAX30102 chip. As usual, if you want the mounting holes in pcb, you need to drag a hole over the pad in silkscreen to actually drill the hole (by default they are not drilled)
